# Fritzing sketch breadboard-diagram (saved by Fritzing 0.9.3b)
breadboards: 1

parts:
  U1 = NodeMCU V1.0
  S1 = Pushbutton [package="[THT]"]
  R1 = Resistor [tolerance=±5% resistance=10k package=THT]

nets:
  N1: U1.D3, S1.Pin_1, S1.Pin_2, R1.Pin_1
  N2: U1.3V3, S1.Pin_3, S1.Pin_4
  N3: U1.GND, R1.Pin_0

custom parts:
  NodeMCU V1.0: ESP8266 based NodeMCU
